// Logisim project battleship.circ as structural Verilog: 3 circuits, main circuit main
module main (
  input  [3:0] Alvo,
  input  [3:0] Navio1,
  input  [3:0] Navio2,
  output out_4,
  output Acertou,
  output Errou,
  output out_7
);

  wire button_1_out, or_1_out;
  wire [3:0] decodificador_1_out_2, decodificador_2_out_2, encoder_1_out_2, encoder_2_out_2;

  Encoder encoder_1 (.in_1(Navio1), .out_2(encoder_1_out_2));
  Encoder encoder_2 (.in_1(Navio2), .out_2(encoder_2_out_2));
  Decodificador decodificador_1 (.in_1(encoder_1_out_2), .out_2(decodificador_1_out_2));
  Decodificador decodificador_2 (.in_1(encoder_2_out_2), .out_2(decodificador_2_out_2));
  Comparator #(.width(4)) comparator_1 (.a(Alvo), .b(decodificador_1_out_2), .eq(out_4));  // open: gt, lt
  Comparator #(.width(4)) comparator_2 (.a(Alvo), .b(decodificador_2_out_2), .eq(out_7));  // open: gt, lt
  Button button_1 (.out(button_1_out));
  or or_1 (or_1_out, out_4, out_7);
  and and_1 (Acertou, or_1_out, button_1_out);
  and and_2 (Errou, button_1_out, ~or_1_out);  // AND_Gate
endmodule

module Encoder (
  input  [3:0] in_1,
  output [3:0] out_2
);

  wire and_1_out, and_2_out, and_3_out, and_4_out, and_5_out, and_6_out, and_7_out, and_8_out, and_9_out,
       and_10_out, and_11_out, and_12_out, and_13_out, and_14_out, and_15_out, and_16_out;

  and and_1 (and_1_out, ~in_1[3], ~in_1[2], in_1[0]);  // AND_Gate
  and and_2 (and_2_out, ~in_1[3], in_1[2], ~in_1[0]);  // AND_Gate
  and and_3 (and_3_out, in_1[3], ~in_1[1], in_1[0]);  // AND_Gate
  and and_4 (and_4_out, in_1[3], in_1[1], ~in_1[0]);  // AND_Gate
  and and_5 (and_5_out, ~in_1[3], ~in_1[2], ~in_1[0]);  // AND_Gate
  and and_6 (and_6_out, ~in_1[3], in_1[1], in_1[0]);  // AND_Gate
  and and_7 (and_7_out, ~in_1[3], in_1[2], ~in_1[1]);  // AND_Gate
  and and_8 (and_8_out, in_1[3], in_1[1], ~in_1[0]);  // AND_Gate
  and and_9 (and_9_out, ~in_1[3], in_1[0]);  // AND_Gate
  and and_10 (and_10_out, in_1[1], in_1[0]);
  and and_11 (and_11_out, in_1[2], in_1[0]);
  and and_12 (and_12_out, ~in_1[3], in_1[2], ~in_1[1]);  // AND_Gate
  and and_13 (and_13_out, ~in_1[2], in_1[1]);  // AND_Gate
  and and_14 (and_14_out, ~in_1[3], in_1[1], ~in_1[0]);  // AND_Gate
  and and_15 (and_15_out, in_1[2], ~in_1[1], in_1[0]);  // AND_Gate
  and and_16 (and_16_out, in_1[3], in_1[2], ~in_1[1]);  // AND_Gate
  or or_1 (out_2[3], and_1_out, and_2_out, and_3_out, and_4_out);
  or or_2 (out_2[2], and_5_out, and_6_out, and_7_out, and_8_out);
  or or_3 (out_2[1], and_9_out, and_10_out, and_11_out, and_12_out);
  or or_4 (out_2[0], and_13_out, and_14_out, and_15_out, and_16_out);
endmodule

module Decodificador (
  input  [3:0] in_1,
  output [3:0] out_2
);

  wire and_1_out, and_2_out, and_3_out, and_4_out, and_5_out, and_6_out, and_7_out, and_8_out, and_9_out,
       and_10_out, and_11_out, and_12_out, and_13_out, and_14_out, and_15_out, and_16_out, and_17_out,
       and_18_out;

  and and_1 (and_1_out, ~in_1[3], ~in_1[2]);  // AND_Gate
  and and_2 (and_2_out, ~in_1[2], ~in_1[1], ~in_1[0]);  // AND_Gate
  and and_3 (and_3_out, ~in_1[2], in_1[1], in_1[0]);  // AND_Gate
  and and_4 (and_4_out, in_1[3], in_1[2], ~in_1[1]);  // AND_Gate
  and and_5 (and_5_out, ~in_1[2], ~in_1[1], in_1[0]);  // AND_Gate
  and and_6 (and_6_out, ~in_1[3], in_1[1], ~in_1[0]);  // AND_Gate
  and and_7 (and_7_out, ~in_1[3], in_1[2], in_1[1]);  // AND_Gate
  and and_8 (and_8_out, in_1[3], ~in_1[2], in_1[1]);  // AND_Gate
  and and_9 (and_9_out, in_1[3], in_1[2], ~in_1[1]);  // AND_Gate
  and and_10 (and_10_out, ~in_1[3], ~in_1[2], in_1[1]);  // AND_Gate
  and and_11 (and_11_out, ~in_1[3], in_1[1], ~in_1[0]);  // AND_Gate
  and and_12 (and_12_out, in_1[2], ~in_1[1], in_1[0]);  // AND_Gate
  and and_13 (and_13_out, in_1[3], ~in_1[1], in_1[0]);  // AND_Gate
  and and_14 (and_14_out, in_1[3], in_1[2], ~in_1[1]);  // AND_Gate
  and and_15 (and_15_out, in_1[3], in_1[2], in_1[0]);
  and and_16 (and_16_out, ~in_1[3], in_1[1]);  // AND_Gate
  and and_17 (and_17_out, in_1[1], in_1[0]);
  and and_18 (and_18_out, in_1[3], ~in_1[2], ~in_1[0]);  // AND_Gate
  or or_1 (out_2[3], and_1_out, and_2_out, and_3_out, and_4_out);
  or or_2 (out_2[1], and_10_out, and_11_out, and_12_out, and_13_out, and_14_out, and_15_out);
  or or_3 (out_2[0], and_16_out, and_17_out, and_18_out);
  or or_4 (out_2[2], and_5_out, and_6_out, and_7_out, and_8_out, and_9_out);
endmodule
